# Fritzing sketch Challenge3Diagram (saved by Fritzing 0.9.3b)
breadboards: 1

parts:
  Part1 = Arduino Uno (Rev3)
  LED1 = LED - 5mm [color="Red (633nm)" package="5 mm [THT]"]
  LED2 = LED - 5mm [color="Blue (430nm)" package="5 mm [THT]"]
  LED3 = LED - 5mm [color="Green (555nm)" package="5 mm [THT]"]

nets:
  N1: Part1.D11_PWM/MOSI, LED3.anode
  N2: Part1.D12/MISO, LED2.anode
  N3: Part1.D13/SCK, LED1.anode
  N4: Part1.GND, LED1.cathode, LED2.cathode, LED3.cathode
